# Fritzing sketch schematic (saved by Fritzing 0.9.2b)
breadboards: 1

parts:
  Part1 = Arduino Mega 2560 (Rev3)
  U1 = MAX6675 [package=so08]
  J1 = Peltier Element
  RHT1 = Humidity and Temperature Sensor RHT03
  U2 = SUP500F [package=sup500f]
  U4 = ESP8266 WiFi Module [part_number=ESP8266]
  IC1 = Voltage Regulator [package=to-220-alt]
  R4 = Temperature Sensor (Thermistor) [thermistor_type=NTC package=THT]
  R5 = Resistor [tolerance=±5% resistance=100k package=THT]
  LED1 = LED - 5mm [color="White (8000K)" package="5 mm [THT]"]
  LED2 = LED - 5mm [color="White (8000K)" package="5 mm [THT]"]
  R1 = Rotary Potentiometer (Small) [maximum_resistance=100kΩ package=THT]
  R3 = Rotary Potentiometer (Small) [maximum_resistance=100kΩ package=THT]
  R2 = Rotary Potentiometer (Small) [maximum_resistance=100kΩ package=THT]
  S2 = Toggle Switch [package=THT]
  S1 = Toggle Switch [package=THT]
  S3 = Toggle Switch [package=THT]
  S4 = Toggle Switch [package=THT]
  R6 = Resistor [tolerance=±5% resistance=10k package=THT]
  R7 = Resistor [tolerance=±5% resistance=10k package=THT]
  R8 = Resistor [tolerance=±5% resistance=10k package=THT]
  R9 = Resistor [tolerance=±5% resistance=10k package=THT]

nets:
  N1: Part1.A0, R1.wiper
  N2: Part1.A1, R2.wiper
  N3: Part1.A2, R3.wiper
  N4: Part1.A3, R4.pin_1, R5.Pin_0
  N5: Part1.D19/RX1, U4.TXD
  N6: Part1.D18/TX1, U4.RXD
  N7: Part1.D17_PWM/RX2, U2.RX-I
  N8: Part1.D16_PWM/TX2, U2.TX-O
  VCC: Part1.5V, U1.VDD, RHT1.Vcc, U2.VCC, IC1.IN, R4.pin_0, R1.leg1, R3.leg1, R2.leg1, S2.L2, S1.L2, S3.L2, S4.L2
  GND: Part1.GND, U1.VSS, RHT1.GND_2, U2.GND, U4.GND, IC1.GND, R5.Pin_1, LED1.cathode, LED2.cathode, R1.leg2, R3.leg2, R2.leg2, R6.Pin_1, R7.Pin_1, R8.Pin_1, R9.Pin_0
  N9: Part1.D2_PWM, RHT1.Data-signal
  N10: Part1.D3_PWM, U1.SCK
  N11: Part1.D4_PWM, U1.CS
  N12: Part1.D5_PWM, U1.MISO
  N13: Part1.D49, LED1.anode, LED2.anode
  N14: Part1.D50, S1.COM, R6.Pin_0
  N15: Part1.D51, S2.COM, R7.Pin_0
  N16: U1.T-, J1.pin2
  N17: U1.T+, J1.pin1
  N18: U4.VCC, IC1.OUT
  N19: S3.COM, R8.Pin_0
  N20: S4.COM, R9.Pin_1

custom parts:
  ESP8266 WiFi Module: Generic WiFi Module based on the ESP8266 with onboard PCB antenna and UART communications
